// Logisim project ALU_18_WIN_final.circ as structural Verilog: 8 circuits, main circuit main
module main (
  input  CTRL0,
  input  CTRL1,
  input  CTRL2,
  input  [17:0] InputA,
  input  [17:0] InputB,
  input  Reseet,
  output [17:0] Result,
  output Zero,
  output Negative,
  output Overflow,
  output Carry,
  output [3:0] Result_35_32,
  output [31:0] Result_31_0
);

  Alu_18 _18_bit_ALU (
    .A(InputA), .B(InputB), .Control0(CTRL0), .Control1(CTRL1), .Result(Result), .Zero(Zero),
    .Negative(Negative), .Overflow(Overflow), .Carry(Carry));
  Booths Boolth_multiplierr (
    .M_input(InputA), .Q_input(InputB), .Reset(Reseet), .Result32(Result_31_0), .Result4(Result_35_32));

  // Notes on the sheet:
  //   0
  //   1
  //   0
  //   1
  //   CTRL0            CTRL1
  //   0
  //   0
  //   OR
  //   1
  //   SUB
  //   1
  //   AND
  //   ADD
endmodule

module And_gate_18 (
  input  [17:0] Input0,
  input  [17:0] Input1,
  output [17:0] out_3
);

  and _1 (out_3[1], Input0[1], Input1[1]);
  and _2 (out_3[2], Input0[2], Input1[2]);
  and _3 (out_3[3], Input0[3], Input1[3]);
  and _4 (out_3[4], Input0[4], Input1[4]);
  and _5 (out_3[5], Input0[5], Input1[5]);
  and _6 (out_3[6], Input0[6], Input1[6]);
  and _7 (out_3[7], Input0[7], Input1[7]);
  and _8 (out_3[8], Input0[8], Input1[8]);
  and _9 (out_3[9], Input0[9], Input1[9]);
  and _10 (out_3[10], Input0[10], Input1[10]);
  and _11 (out_3[11], Input0[11], Input1[11]);
  and _12 (out_3[12], Input0[12], Input1[12]);
  and _13 (out_3[13], Input0[13], Input1[13]);
  and _14 (out_3[14], Input0[14], Input1[14]);
  and _15 (out_3[15], Input0[15], Input1[15]);
  and _16 (out_3[16], Input0[16], Input1[16]);
  and _17 (out_3[17], Input0[17], Input1[17]);
  and _0 (out_3[0], Input0[0], Input1[0]);

  // Notes on the sheet:
  //   AND Gate 18 Bit
endmodule

module Or_Gate_18 (
  input  [17:0] Input0,
  input  [17:0] Input1,
  output [17:0] out_3
);

  or or_1 (out_3[1], Input0[1], Input1[1]);
  or or_2 (out_3[2], Input0[2], Input1[2]);
  or or_3 (out_3[3], Input0[3], Input1[3]);
  or or_4 (out_3[4], Input0[4], Input1[4]);
  or or_5 (out_3[5], Input0[5], Input1[5]);
  or or_6 (out_3[6], Input0[6], Input1[6]);
  or or_7 (out_3[7], Input0[7], Input1[7]);
  or or_8 (out_3[8], Input0[8], Input1[8]);
  or or_9 (out_3[9], Input0[9], Input1[9]);
  or or_10 (out_3[10], Input0[10], Input1[10]);
  or or_11 (out_3[11], Input0[11], Input1[11]);
  or or_12 (out_3[12], Input0[12], Input1[12]);
  or or_13 (out_3[13], Input0[13], Input1[13]);
  or or_14 (out_3[14], Input0[14], Input1[14]);
  or or_15 (out_3[15], Input0[15], Input1[15]);
  or or_16 (out_3[16], Input0[16], Input1[16]);
  or or_17 (out_3[17], Input0[17], Input1[17]);
  or or_18 (out_3[0], Input0[0], Input1[0]);

  // Notes on the sheet:
  //   OR Gate 18 Bit
endmodule

// FA
module Full_Adder_1 (
  input  Carry_In,
  input  Input0,
  input  Input1,
  output Sum,
  output Carry_Out
);

  wire and_1_out, and_2_out, xor_1_out;

  and and_1 (and_1_out, Input1, Input0);
  xor xor_1 (xor_1_out, Input0, Input1);
  or or_1 (Carry_Out, and_1_out, and_2_out);
  and and_2 (and_2_out, xor_1_out, Carry_In);
  xor xor_2 (Sum, xor_1_out, Carry_In);
endmodule

module Full_Adder_18 (
  input  CTRL,
  input  [17:0] Input0,
  input  [17:0] Input1,
  output [17:0] Result,
  output Carry,
  output Overflow
);

  wire and_1_out, and_2_out, full_adder_1_1_carry_out, full_adder_1_2_carry_out, full_adder_1_3_carry_out,
       full_adder_1_4_carry_out, full_adder_1_5_carry_out, full_adder_1_6_carry_out,
       full_adder_1_7_carry_out, full_adder_1_8_carry_out, full_adder_1_9_carry_out,
       full_adder_1_10_carry_out, full_adder_1_11_carry_out, full_adder_1_12_carry_out,
       full_adder_1_13_carry_out, full_adder_1_14_carry_out, full_adder_1_15_carry_out,
       full_adder_1_16_carry_out, full_adder_1_17_carry_out, not_1_out, not_2_out, not_3_out, xor_1_out,
       xor_2_out, xor_3_out, xor_4_out, xor_5_out, xor_6_out, xor_7_out, xor_8_out, xor_9_out, xor_10_out,
       xor_11_out, xor_12_out, xor_13_out, xor_14_out, xor_15_out, xor_16_out, xor_17_out, xor_18_out;

  xor xor_1 (xor_1_out, CTRL, Input1[0]);
  xor xor_2 (xor_2_out, CTRL, Input1[1]);
  xor xor_3 (xor_3_out, CTRL, Input1[2]);
  xor xor_4 (xor_4_out, CTRL, Input1[3]);
  xor xor_5 (xor_5_out, CTRL, Input1[4]);
  xor xor_6 (xor_6_out, CTRL, Input1[5]);
  xor xor_7 (xor_7_out, CTRL, Input1[6]);
  xor xor_8 (xor_8_out, CTRL, Input1[7]);
  xor xor_9 (xor_9_out, CTRL, Input1[8]);
  xor xor_10 (xor_10_out, CTRL, Input1[9]);
  xor xor_11 (xor_11_out, CTRL, Input1[10]);
  xor xor_12 (xor_12_out, CTRL, Input1[11]);
  xor xor_13 (xor_13_out, CTRL, Input1[12]);
  xor xor_14 (xor_14_out, CTRL, Input1[13]);
  xor xor_15 (xor_15_out, CTRL, Input1[14]);
  xor xor_16 (xor_16_out, CTRL, Input1[15]);
  xor xor_17 (xor_17_out, CTRL, Input1[16]);
  xor xor_18 (xor_18_out, CTRL, Input1[17]);
  Full_Adder_1 full_adder_1_1 (
    .Input0(Input0[0]), .Input1(xor_1_out), .Carry_In(CTRL), .Carry_Out(full_adder_1_1_carry_out),
    .Sum(Result[0]));
  Full_Adder_1 full_adder_1_2 (
    .Input0(Input0[1]), .Input1(xor_2_out), .Carry_In(full_adder_1_1_carry_out),
    .Carry_Out(full_adder_1_2_carry_out), .Sum(Result[1]));
  Full_Adder_1 full_adder_1_3 (
    .Input0(Input0[2]), .Input1(xor_3_out), .Carry_In(full_adder_1_2_carry_out),
    .Carry_Out(full_adder_1_3_carry_out), .Sum(Result[2]));
  Full_Adder_1 full_adder_1_4 (
    .Input0(Input0[3]), .Input1(xor_4_out), .Carry_In(full_adder_1_3_carry_out),
    .Carry_Out(full_adder_1_4_carry_out), .Sum(Result[3]));
  Full_Adder_1 full_adder_1_5 (
    .Input0(Input0[4]), .Input1(xor_5_out), .Carry_In(full_adder_1_4_carry_out),
    .Carry_Out(full_adder_1_5_carry_out), .Sum(Result[4]));
  Full_Adder_1 full_adder_1_6 (
    .Input0(Input0[5]), .Input1(xor_6_out), .Carry_In(full_adder_1_5_carry_out),
    .Carry_Out(full_adder_1_6_carry_out), .Sum(Result[5]));
  Full_Adder_1 full_adder_1_7 (
    .Input0(Input0[6]), .Input1(xor_7_out), .Carry_In(full_adder_1_6_carry_out),
    .Carry_Out(full_adder_1_7_carry_out), .Sum(Result[6]));
  Full_Adder_1 full_adder_1_8 (
    .Input0(Input0[7]), .Input1(xor_8_out), .Carry_In(full_adder_1_7_carry_out),
    .Carry_Out(full_adder_1_8_carry_out), .Sum(Result[7]));
  Full_Adder_1 full_adder_1_9 (
    .Input0(Input0[8]), .Input1(xor_9_out), .Carry_In(full_adder_1_8_carry_out),
    .Carry_Out(full_adder_1_9_carry_out), .Sum(Result[8]));
  Full_Adder_1 full_adder_1_10 (
    .Input0(Input0[9]), .Input1(xor_10_out), .Carry_In(full_adder_1_9_carry_out),
    .Carry_Out(full_adder_1_10_carry_out), .Sum(Result[9]));
  Full_Adder_1 full_adder_1_11 (
    .Input0(Input0[10]), .Input1(xor_11_out), .Carry_In(full_adder_1_10_carry_out),
    .Carry_Out(full_adder_1_11_carry_out), .Sum(Result[10]));
  Full_Adder_1 full_adder_1_12 (
    .Input0(Input0[11]), .Input1(xor_12_out), .Carry_In(full_adder_1_11_carry_out),
    .Carry_Out(full_adder_1_12_carry_out), .Sum(Result[11]));
  Full_Adder_1 full_adder_1_13 (
    .Input0(Input0[12]), .Input1(xor_13_out), .Carry_In(full_adder_1_12_carry_out),
    .Carry_Out(full_adder_1_13_carry_out), .Sum(Result[12]));
  Full_Adder_1 full_adder_1_14 (
    .Input0(Input0[13]), .Input1(xor_14_out), .Carry_In(full_adder_1_13_carry_out),
    .Carry_Out(full_adder_1_14_carry_out), .Sum(Result[13]));
  Full_Adder_1 full_adder_1_15 (
    .Input0(Input0[14]), .Input1(xor_15_out), .Carry_In(full_adder_1_14_carry_out),
    .Carry_Out(full_adder_1_15_carry_out), .Sum(Result[14]));
  Full_Adder_1 full_adder_1_16 (
    .Input0(Input0[15]), .Input1(xor_16_out), .Carry_In(full_adder_1_15_carry_out),
    .Carry_Out(full_adder_1_16_carry_out), .Sum(Result[15]));
  Full_Adder_1 full_adder_1_17 (
    .Input0(Input0[16]), .Input1(xor_17_out), .Carry_In(full_adder_1_16_carry_out),
    .Carry_Out(full_adder_1_17_carry_out), .Sum(Result[16]));
  Full_Adder_1 full_adder_1_18 (
    .Input0(Input0[17]), .Input1(xor_18_out), .Carry_In(full_adder_1_17_carry_out), .Carry_Out(Carry),
    .Sum(Result[17]));
  not not_1 (not_1_out, Result[17]);
  not not_2 (not_2_out, Input0[17]);
  not not_3 (not_3_out, xor_18_out);
  and and_1 (and_1_out, Input0[17], not_1_out, xor_18_out);
  and and_2 (and_2_out, not_2_out, not_3_out, Result[17]);
  or or_1 (Overflow, and_1_out, and_2_out);

  // Notes on the sheet:
  //   FULL Adder 18 Bit
  //   0 = Addition
  //   1 = Subtraction
endmodule

module Alu_18 (
  input  Control0,
  input  Control1,
  input  [17:0] A,
  input  [17:0] B,
  output [17:0] Result,
  output Zero,
  output Negative,
  output Overflow,
  output Carry
);

  wire or_2_out;
  wire [17:0] AND_out_3, FA_result, multiplexer_1_out, OR_out_3;

  And_gate_18 AND (.Input0(A), .Input1(B), .out_3(AND_out_3));
  Or_Gate_18 OR (.Input0(A), .Input1(B), .out_3(OR_out_3));
  Full_Adder_18 FA (.Input1(B), .CTRL(Control0), .Input0(A), .Result(FA_result), .Carry(Carry), .Overflow(Overflow));
  Multiplexer #(.width(18), .enable("false")) multiplexer_1 (
    .in0(AND_out_3), .in1(OR_out_3), .out(multiplexer_1_out), .sel(Control0));
  Multiplexer #(.width(18), .enable("false")) multiplexer_2 (
    .in0(multiplexer_1_out), .in1(FA_result), .out({Negative, Result[16:0]}), .sel(Control1));
  or or_2 (or_2_out, Result[0], Result[1], Result[2], Result[3], Result[4], Result[5], Result[6], Result[7], Result[8], Result[9], Result[10], Result[11], Result[12], Result[13], Result[14], Result[15], Result[16], Negative);
  not not_1 (Zero, or_2_out);

  assign Result[17] = Negative;
endmodule

module Booths (
  input  [17:0] M_input,
  input  [17:0] Q_input,
  input  Reset,
  output [31:0] Result32,
  output [3:0] Result4
);

  wire A_out, clock_1_out, controlller_1_c0, controlller_1_c1, controlller_1_dec_cnt,
       controlller_1_load__m__q__cnt, controlller_1_load_a, controlller_1_shr, or_1_out, Q_1_q0, Q_out;
  wire [4:0] counter_1_q;
  wire [17:0] ALU_18_result, M_q17;

  Controlller controlller_1 (
    .Clk(clock_1_out), .Reset(Reset), .Q0(Result32[0]), .Q_1(Q_1_q0), .Count(counter_1_q),
    .Cl__A__Q_1(Result32[21]), .LOad__M__Q__Cnt(controlller_1_load__m__q__cnt),
    .Load_A(controlller_1_load_a), .C0(controlller_1_c0), .C1(controlller_1_c1), .Shr(controlller_1_shr),
    .Dec_Cnt(controlller_1_dec_cnt));
  Clock clock_1 (.out(clock_1_out));
  or or_1 (or_1_out, controlller_1_load__m__q__cnt, controlller_1_dec_cnt);
  Counter #(.width(5), .max('h12)) counter_1 (
    .load(or_1_out), .D(5'b11000), .count(controlller_1_dec_cnt), .Q(counter_1_q), .clk(clock_1_out));  // open: carry, clr
  Alu_18 ALU_18 (
    .A({Result4, Result32[31:18]}), .B(M_q17), .Control0(controlller_1_c0), .Control1(controlller_1_c1),
    .Result(ALU_18_result));  // open: Zero, Negative, Overflow, Carry
  Shift_Register #(.length(18)) M (
    .shift(1'b0), .clk(clock_1_out), .load(controlller_1_load__m__q__cnt), .d0(M_input[17]), .q0(M_q17[17]),
    .d1(M_input[16]), .q1(M_q17[16]), .d2(M_input[15]), .q2(M_q17[15]), .d3(M_input[14]), .q3(M_q17[14]),
    .d4(M_input[13]), .q4(M_q17[13]), .d5(M_input[12]), .q5(M_q17[12]), .d6(M_input[11]), .q6(M_q17[11]),
    .d7(M_input[10]), .q7(M_q17[10]), .d8(M_input[9]), .q8(M_q17[9]), .d9(M_input[8]), .q9(M_q17[8]),
    .d10(M_input[7]), .q10(M_q17[7]), .d11(M_input[6]), .q11(M_q17[6]), .d12(M_input[5]), .q12(M_q17[5]),
    .d13(M_input[4]), .q13(M_q17[4]), .d14(M_input[3]), .q14(M_q17[3]), .d15(M_input[2]), .q15(M_q17[2]),
    .d16(M_input[1]), .q16(M_q17[1]), .d17(M_input[0]), .q17(M_q17[0]));  // open: in, out, clr
  Shift_Register #(.length(18)) A (
    .shift(controlller_1_shr), .in(Result4[3]), .clk(clock_1_out), .out(A_out), .load(controlller_1_load_a),
    .clr(Result32[21]), .d0(ALU_18_result[17]), .q0(Result4[3]), .d1(ALU_18_result[16]), .q1(Result4[2]),
    .d2(ALU_18_result[15]), .q2(Result4[1]), .d3(ALU_18_result[14]), .q3(Result4[0]), .d4(ALU_18_result[13]),
    .q4(Result32[31]), .d5(ALU_18_result[12]), .q5(Result32[30]), .d6(ALU_18_result[11]), .q6(Result32[29]),
    .d7(ALU_18_result[10]), .q7(Result32[28]), .d8(ALU_18_result[9]), .q8(Result32[27]),
    .d9(ALU_18_result[8]), .q9(Result32[26]), .d10(ALU_18_result[7]), .q10(Result32[25]),
    .d11(ALU_18_result[6]), .q11(Result32[24]), .d12(ALU_18_result[5]), .q12(Result32[23]),
    .d13(ALU_18_result[4]), .q13(Result32[22]), .d14(ALU_18_result[3]), .q14(Result32[21]),
    .d15(ALU_18_result[2]), .q15(Result32[20]), .d16(ALU_18_result[1]), .q16(Result32[19]),
    .d17(ALU_18_result[0]), .q17(Result32[18]));
  Shift_Register #(.length(18)) Q (
    .shift(controlller_1_shr), .in(A_out), .clk(clock_1_out), .out(Q_out),
    .load(controlller_1_load__m__q__cnt), .d0(Q_input[17]), .q0(Result32[17]), .d1(Q_input[16]),
    .q1(Result32[16]), .d2(Q_input[15]), .q2(Result32[15]), .d3(Q_input[14]), .q3(Result32[14]),
    .d4(Q_input[13]), .q4(Result32[13]), .d5(Q_input[12]), .q5(Result32[12]), .d6(Q_input[11]),
    .q6(Result32[11]), .d7(Q_input[10]), .q7(Result32[10]), .d8(Q_input[9]), .q8(Result32[9]),
    .d9(Q_input[8]), .q9(Result32[8]), .d10(Q_input[7]), .q10(Result32[7]), .d11(Q_input[6]),
    .q11(Result32[6]), .d12(Q_input[5]), .q12(Result32[5]), .d13(Q_input[4]), .q13(Result32[4]),
    .d14(Q_input[3]), .q14(Result32[3]), .d15(Q_input[2]), .q15(Result32[2]), .d16(Q_input[1]),
    .q16(Result32[1]), .d17(Q_input[0]), .q17(Result32[0]));  // open: clr
  Shift_Register #(.length(1)) Q_1 (
    .shift(controlller_1_shr), .in(Q_out), .clk(clock_1_out), .clr(Result32[21]), .q0(Q_1_q0));  // open: out, load, d0
endmodule

module Controlller (
  input  Clk,
  input  Reset,
  input  Q0,
  input  Q_1,
  input  [4:0] Count,
  output Cl__A__Q_1,
  output LOad__M__Q__Cnt,
  output Load_A,
  output C0,
  output C1,
  output Shr,
  output Dec_Cnt
);

  wire and_3_out, multiplexer_1_out, not_1_out, not_2_out, not_3_out, not_4_out, not_5_out, not_6_out,
       not_7_out, or_2_out, Q0_prime_Q_1_out, Q0Q_1_prime_out;
  wire [1:0] rom_1_data_2;
  wire [2:0] and_1_out, and_2_out, bit_extender_1_out, bit_extender_2_out, bit_extender_3_out, CAR_q,
       or_1_out, rom_1_data;

  assign bit_extender_1_out = {{2{Q0_prime_Q_1_out}}, Q0_prime_Q_1_out};  // Bit_Extender bit_extender_1
  and Q0_prime_Q_1 (Q0_prime_Q_1_out, not_2_out, Q_1);
  not not_1 (not_1_out, Q0_prime_Q_1_out);
  assign bit_extender_2_out = {{2{not_1_out}}, not_1_out};  // Bit_Extender bit_extender_2
  assign and_1_out = 3'b100 & bit_extender_3_out & bit_extender_1_out;  // AND_Gate and_1, 3 bits wide
  assign or_1_out = and_1_out | rom_1_data | and_2_out;  // OR_Gate or_1, 3 bits wide
  not not_2 (not_2_out, Q0);
  assign and_2_out = bit_extender_2_out & bit_extender_3_out & 3'b101;  // AND_Gate and_2, 3 bits wide
  assign bit_extender_3_out = {{2{and_3_out}}, and_3_out};  // Bit_Extender bit_extender_3
  and and_3 (and_3_out, not_3_out, CAR_q[1], not_4_out);
  not not_3 (not_3_out, CAR_q[2]);
  not not_4 (not_4_out, CAR_q[0]);
  Counter #(.width(3), .max('h7)) CAR (
    .load(not_5_out), .D(or_1_out), .count(multiplexer_1_out), .Q(CAR_q), .clk(Clk), .clr(Reset));  // open: carry
  not not_5 (not_5_out, multiplexer_1_out);
  Multiplexer #(.select(2), .enable("false")) multiplexer_1 (
    .in0(1'b0), .in1(1'b1), .in2(Q0Q_1_prime_out), .in3(not_7_out), .out(multiplexer_1_out),
    .sel(rom_1_data_2));
  ROM #(.addrWidth(3), .dataWidth(12)) rom_1 (
    .addr(CAR_q), .data({Cl__A__Q_1, LOad__M__Q__Cnt, Load_A, C0, C1, Shr, Dec_Cnt, rom_1_data, rom_1_data_2}));  // open: sel
  and Q0Q_1_prime (Q0Q_1_prime_out, not_6_out, Q0);
  not not_6 (not_6_out, Q_1);
  not not_7 (not_7_out, or_2_out);
  or or_2 (or_2_out, Count[0], Count[1], Count[2], Count[3], Count[4]);

  // Notes on the sheet:
  //   To choose only
  //   state 2 (010)
  //   Control Word Format: Clear (A, Q-1), Load (M, Q, Cnt), Load A, C0, C1, Shr, Dec Cnt, Address bits (3 bit), Selection bits (2 bit)
  //   contents of rom_1 (hex, n*v repeats v):
  //   1 c01 2 394 281 61 b 1c
endmodule
